// Logisim project lab06.circ as structural Verilog: 28 circuits, main circuit mcpfull
module mcpfull (
);

  wire AdrSrc, clock_1_out, clock_2_out, clock_3_out, clock_4_out, clock_5_out, clock_6_out, clock_7_out,
       clock_8_out, clock_9_out, clock_10_out, clock_11_out, Funct7_5, IRWrite, MemWrite, PCWrite, RegWrite,
       SignedLess, UnsignedLess, Zero;
  wire [1:0] ALUSrcA, ALUSrcB, ResultSrc;
  wire [2:0] ALUControl, Funct3, ImmSrc;
  wire [3:0] controlunit_1_state;
  wire [4:0] Rd, Rs1, Rs2;
  wire [6:0] Op;
  wire [15:0] Ticks;
  wire [24:0] instsplitter_1_instr31_7;
  wire [31:0] A_out_5, Addr, ALUOut, ALUResult, B_out_5, constant4_1_out_1, Data, ImmExt, Instr, LoadData,
       OldPC, PC, RD1, RD2, ReadData, Result, SrcA, SrcB, StoreData;

  // Probe on PC
  // Probe on Addr
  // Probe on ReadData
  Clock clock_1 (.out(clock_1_out));
  reg32 u_PC (.WE(PCWrite), .CLK(clock_1_out), .in_1(Result), .out_5(PC));  // open: CLR
  // Probe on PCWrite
  Clock clock_2 (.out(clock_2_out));
  // Probe on PCWrite
  // Probe on MemWrite
  // Probe on IRWrite
  // Probe on AdrSrc
  // Probe on AdrSrc
  mux2 mux2_1 (.A(PC), .B(Result), .Sel(AdrSrc), .Selected(Addr));
  Counter #(.max('hffff), .width(16)) counter_1 (.Q(Ticks), .clk(clock_2_out));  // open: load, D, count, carry, up, clr
  // Probe on Addr[1:0]
  // Probe on OldPC
  // Probe on Instr
  // Probe on Data
  // Probe on Op
  // Probe on Rs1
  // Probe on Rs2
  // Probe on Rd
  // Probe on Funct3
  // Probe on Funct7_5
  // Probe on MemWrite
  Clock clock_3 (.out(clock_3_out));
  idmem idmem_1 (.A(Addr), .WD(StoreData), .CLK(clock_3_out), .WE(MemWrite), .ReadData(ReadData));
  Clock clock_4 (.out(clock_4_out));
  reg32 u_OldPC (.WE(IRWrite), .CLK(clock_4_out), .in_1(PC), .out_5(OldPC));  // open: CLR
  // Probe on IRWrite
  Clock clock_5 (.out(clock_5_out));
  reg32 u_Instr (.WE(IRWrite), .CLK(clock_5_out), .in_1(ReadData), .out_5(Instr));  // open: CLR
  // Probe on IRWrite
  // Probe on ReadData
  Clock clock_6 (.out(clock_6_out));
  reg32 u_Data (.WE(1'b1), .CLK(clock_6_out), .in_1(ReadData), .out_5(Data));  // open: CLR
  // Probe on Data
  // Probe on ImmExt
  // Probe on RD1
  // Probe on RD2
  instsplitter instsplitter_1 (
    .Instr(Instr), .Instr6_0(Op), .Instr14_12(Funct3), .Instr30(Funct7_5), .Instr19_15(Rs1),
    .Instr24_20(Rs2), .Instr11_7(Rd), .Instr31_7(instsplitter_1_instr31_7));
  // Probe on LoadData
  LoadFormatter loadformatter_1 (.MemData(Data), .Addr_1_0(Addr[1:0]), .Funct3(Funct3), .LoadData(LoadData));
  // Probe on Ticks
  // Probe on RegWrite
  // Probe on ImmSrc
  // Probe on RegWrite
  Clock clock_7 (.out(clock_7_out));
  // Probe on ImmSrc
  Clock clock_8 (.out(clock_8_out));
  reg32 A (.WE(1'b1), .CLK(clock_8_out), .in_1(RD1), .out_5(A_out_5));  // open: CLR
  regfile regfile_1 (
    .A1(Rs1), .A2(Rs2), .A3(Rd), .WD3(Result), .CLK(clock_7_out), .WE3(RegWrite), .RD1(RD1), .RD2(RD2));
  Clock clock_9 (.out(clock_9_out));
  reg32 B (.WE(1'b1), .CLK(clock_9_out), .in_1(RD2), .out_5(B_out_5));  // open: CLR
  extend extend_1 (.Instr31_7(instsplitter_1_instr31_7), .ImmSrc(ImmSrc), .ImmExt(ImmExt));
  // Probe on LoadData
  // Probe on SrcA
  // Probe on SrcB
  // Probe on ALUResult
  // Probe on ALUOut
  // Probe on Result
  // Probe on ALUSrcA
  // Probe on ALUSrcB
  // Probe on ALUControl
  // Probe on ResultSrc
  // Probe on ALUSrcA
  mux3 mux3_1 (.A(PC), .B(OldPC), .C(A_out_5), .Sel(ALUSrcA), .Selected(SrcA));
  // Probe on ALUSrcB
  // Probe on B_out_5
  constant4 constant4_1 (.out_1(constant4_1_out_1));
  // Probe on ALUControl
  alu alu_1 (
    .SrcB(SrcB), .ALUControl(ALUControl), .SrcA(SrcA), .Funct3(Funct3), .Funct7_5(Funct7_5),
    .ALUResult(ALUResult), .SignedLess(SignedLess), .UnsignedLess(UnsignedLess), .Zero(Zero));
  mux3 mux3_2 (.A(B_out_5), .B(ImmExt), .C(constant4_1_out_1), .Sel(ALUSrcB), .Selected(SrcB));
  // Probe on ImmExt
  Clock clock_10 (.out(clock_10_out));
  // Probe on controlunit_1_state
  // Probe on Zero
  Clock clock_11 (.out(clock_11_out));
  reg32 u_ALUOut (.WE(1'b1), .CLK(clock_11_out), .in_1(ALUResult), .out_5(ALUOut));  // open: CLR
  // Probe on ALUResult
  // Probe on Result
  controlunit controlunit_1 (
    .funct3(Funct3), .funct7_5(Funct7_5), .Zero(Zero), .CLK(clock_10_out), .SignedLess(SignedLess),
    .UnsignedLess(UnsignedLess), .opcode(Op), .MemWrite(MemWrite), .RegWrite(RegWrite), .AdrSrc(AdrSrc),
    .ALUSrcA(ALUSrcA), .ALUSrcB(ALUSrcB), .ALUControl(ALUControl), .ImmSrc(ImmSrc), .ResultSrc(ResultSrc),
    .State(controlunit_1_state), .PCWrite(PCWrite), .IRWrite(IRWrite));
  Multiplexer #(.enable("true"), .select(2), .width(32)) multiplexer_1 (
    .in0(ALUOut), .in1(LoadData), .in2(ALUResult), .in3(ImmExt), .out(Result), .sel(ResultSrc));  // open: en
  // Probe on StoreData
  StoreFormatter storeformatter_1 (
    .MemData(Data), .WriteData(RD2), .Addr_1_0(Addr[1:0]), .Funct3(Funct3), .StoreData(StoreData));
  // Probe on ResultSrc
endmodule

module mcppartial (
  input  in_1,
  input  [1:0] in_2,
  input  in_3,
  input  [1:0] in_4,
  input  in_5,
  input  in_6,
  input  [2:0] in_7,
  input  in_8,
  input  [2:0] in_9,
  input  [1:0] in_10
);

  wire clock_1_out, clock_2_out, clock_3_out, clock_4_out, clock_5_out, clock_6_out, clock_7_out,
       clock_8_out, clock_9_out, clock_10_out, Funct7_5, Zero;
  wire [2:0] Funct3;
  wire [4:0] Rd, Rs1, Rs2;
  wire [6:0] Op;
  wire [15:0] Ticks;
  wire [24:0] instsplitter_1_instr31_7;
  wire [31:0] A_out_5, Addr, ALUOut, ALUResult, B_out_5, constant4_1_out_1, Data, ImmExt, Instr, OldPC, PC,
       RD1, RD2, ReadData, Result, SrcA, SrcB;

  // Probe on PC
  // Probe on Addr
  // Probe on ReadData
  Clock clock_1 (.out(clock_1_out));
  reg32 u_PC (.WE(in_1), .CLK(clock_1_out), .in_1(Result), .out_5(PC));  // open: CLR
  // Probe on in_1
  Clock clock_2 (.out(clock_2_out));
  // Probe on in_1
  // Probe on in_3
  // Probe on in_5
  // Probe on in_8
  // Probe on in_8
  mux2 mux2_1 (.A(PC), .B(Result), .Sel(in_8), .Selected(Addr));
  Counter #(.max('hffff), .width(16)) counter_1 (.Q(Ticks), .clk(clock_2_out));  // open: load, D, count, carry, up, clr
  // Probe on OldPC
  // Probe on Instr
  // Probe on Data
  // Probe on Op
  // Probe on Rs1
  // Probe on Rs2
  // Probe on Rd
  // Probe on Funct3
  // Probe on Funct7_5
  // Probe on in_3
  Clock clock_3 (.out(clock_3_out));
  idmem idmem_1 (.A(Addr), .WD(B_out_5), .CLK(clock_3_out), .WE(in_3), .ReadData(ReadData));
  Clock clock_4 (.out(clock_4_out));
  reg32 u_OldPC (.WE(in_5), .CLK(clock_4_out), .in_1(PC), .out_5(OldPC));  // open: CLR
  // Probe on in_5
  Clock clock_5 (.out(clock_5_out));
  reg32 u_Instr (.WE(in_5), .CLK(clock_5_out), .in_1(ReadData), .out_5(Instr));  // open: CLR
  // Probe on in_5
  Clock clock_6 (.out(clock_6_out));
  reg32 u_Data (.WE(1'b1), .CLK(clock_6_out), .in_1(ReadData), .out_5(Data));  // open: CLR
  // Probe on ImmExt
  // Probe on RD1
  // Probe on RD2
  instsplitter instsplitter_1 (
    .Instr(Instr), .Instr6_0(Op), .Instr14_12(Funct3), .Instr30(Funct7_5), .Instr19_15(Rs1),
    .Instr24_20(Rs2), .Instr11_7(Rd), .Instr31_7(instsplitter_1_instr31_7));
  // Probe on Ticks
  // Probe on in_6
  // Probe on in_9
  // Probe on in_6
  Clock clock_7 (.out(clock_7_out));
  // Probe on in_9
  Clock clock_8 (.out(clock_8_out));
  reg32 A (.WE(1'b1), .CLK(clock_8_out), .in_1(RD1), .out_5(A_out_5));  // open: CLR
  regfile regfile_1 (.A1(Rs1), .A2(Rs2), .A3(Rd), .WD3(Result), .CLK(clock_7_out), .WE3(in_6), .RD1(RD1), .RD2(RD2));
  Clock clock_9 (.out(clock_9_out));
  reg32 B (.WE(1'b1), .CLK(clock_9_out), .in_1(RD2), .out_5(B_out_5));  // open: CLR
  extend extend_1 (.Instr31_7(instsplitter_1_instr31_7), .ImmSrc(in_9), .ImmExt(ImmExt));
  // Probe on SrcA
  // Probe on SrcB
  // Probe on ALUResult
  // Probe on ALUOut
  // Probe on Result
  // Probe on in_2
  // Probe on in_4
  // Probe on in_7
  // Probe on in_10
  // Probe on in_2
  mux3 mux3_1 (.A(PC), .B(OldPC), .C(A_out_5), .Sel(in_2), .Selected(SrcA));
  // Probe on in_4
  constant4 constant4_1 (.out_1(constant4_1_out_1));
  // Probe on in_7
  alu alu_1 (
    .SrcB(SrcB), .ALUControl(in_7), .SrcA(SrcA), .ALUResult(ALUResult), .Zero(Zero));  // open: Funct3, Funct7_5, SignedLess, UnsignedLess
  mux3 mux3_2 (.A(B_out_5), .B(ImmExt), .C(constant4_1_out_1), .Sel(in_4), .Selected(SrcB));
  // Probe on Zero
  Clock clock_10 (.out(clock_10_out));
  reg32 u_ALUOut (.WE(1'b1), .CLK(clock_10_out), .in_1(ALUResult), .out_5(ALUOut));  // open: CLR
  // Probe on in_10
  mux3 mux3_3 (.A(ALUOut), .B(Data), .C(ALUResult), .Sel(in_10), .Selected(Result));

  // Other names for the same wires on the sheet: AdrSrc = in_8; ALUControl[2:0] = in_7; ALUSrcA[1:0] = in_2;
  //   ALUSrcB[1:0] = in_4; ImmSrc[2:0] = in_9; IRWrite = in_5; MemWrite = in_3; PCWrite = in_1; RegWrite = in_6;
  //   ResultSrc[1:0] = in_10
endmodule

module controlunit (
  input  CLK,
  input  [6:0] opcode,
  input  [2:0] funct3,
  input  funct7_5,
  input  Zero,
  input  SignedLess,
  input  UnsignedLess,
  output PCWrite,
  output IRWrite,
  output MemWrite,
  output RegWrite,
  output AdrSrc,
  output [1:0] ALUSrcA,
  output [1:0] ALUSrcB,
  output [2:0] ALUControl,
  output [2:0] ImmSrc,
  output [1:0] ResultSrc,
  output [3:0] State
);

  wire Branch, BranchTaken, PCUpdate;
  wire [1:0] ALUOp;
  wire [3:0] NextState;

  Register #(.width(4)) StateReg (.D(NextState), .clk(CLK), .Q(State));  // open: en, clr
  nextstatelogic nextstatelogic_1 (.opcode(opcode), .State(State), .funct3(funct3), .NextState(NextState));
  aludecoder aludecoder_1 (
    .funct7_5(funct7_5), .funct3(funct3), .ALUOp(ALUOp), .opcode(opcode), .ALUControl(ALUControl));
  instrdecoder instrdecoder_1 (.opcode(opcode), .ImmSrc(ImmSrc));
  BranchLogic branchlogic_1 (
    .Branch(Branch), .Zero(Zero), .SignedLess(SignedLess), .UnsignedLess(UnsignedLess), .Funct3(funct3),
    .BranchTaken(BranchTaken));
  maindecoder maindecoder_1 (
    .state(State), .PCUpdate(PCUpdate), .Branch(Branch), .MemWrite(MemWrite), .IRWrite(IRWrite),
    .RegWrite(RegWrite), .AdrSrc(AdrSrc), .ALUSrcA(ALUSrcA), .ALUSrcB(ALUSrcB), .ResultSrc(ResultSrc),
    .ALUOp(ALUOp));
  // Probe on PCUpdate
  // Probe on Branch
  // Probe on MemWrite
  // Probe on IRWrite
  // Probe on RegWrite
  // Probe on AdrSrc
  // Probe on ALUSrcA
  // Probe on ALUSrcB
  // Probe on ResultSrc
  // Probe on ALUOp
  or or_1 (PCWrite, BranchTaken, PCUpdate);
endmodule

module datamem (
  input  CLK,
  input  WE,
  input  [31:0] A,
  input  [31:0] WD,
  output [31:0] ReadData
);

  RAM #(.addrWidth(24), .asyncread("true"), .dataWidth(32)) DataMem (
    .addr(A[25:2]), .we(WE), .oe(1'b1), .clk(CLK), .din(WD), .dout(ReadData));

  // Other names for the same wires on the sheet: A_t[23:0] = A[25:2]
endmodule

module idmem (
  input  CLK,
  input  WE,
  input  [31:0] A,
  input  [31:0] WD,
  output [31:0] ReadData
);

  RAM #(.addrWidth(24), .asyncread("true"), .dataWidth(32)) DataMem (
    .addr(A[25:2]), .we(WE), .oe(1'b1), .clk(CLK), .din(WD), .dout(ReadData));

  // Other names for the same wires on the sheet: A_t[23:0] = A[25:2]
endmodule

module constant4 (
  output [31:0] out_1
);


  assign out_1 = 32'h4;
endmodule

module reg1 (
  input  in_1,
  input  WE,
  input  CLK,
  input  CLR,
  output out_5
);

  Register #(.width(1)) register_1 (.D(in_1), .en(WE), .clk(CLK), .Q(out_5), .clr(CLR));
endmodule

module reg2 (
  input  [1:0] in_1,
  input  WE,
  input  CLK,
  input  CLR,
  output [1:0] out_5
);

  Register #(.width(2)) register_1 (.D(in_1), .en(WE), .clk(CLK), .Q(out_5), .clr(CLR));
endmodule

module reg3 (
  input  [2:0] in_1,
  input  WE,
  input  CLK,
  input  CLR,
  output [2:0] out_5
);

  Register #(.width(3)) register_1 (.D(in_1), .en(WE), .clk(CLK), .Q(out_5), .clr(CLR));
endmodule

module reg5 (
  input  [4:0] in_1,
  input  WE,
  input  CLK,
  input  CLR,
  output [4:0] out_5
);

  Register #(.width(5)) register_1 (.D(in_1), .en(WE), .clk(CLK), .Q(out_5), .clr(CLR));
endmodule

module reg32 (
  input  [31:0] in_1,
  input  WE,
  input  CLK,
  input  CLR,
  output [31:0] out_5
);

  Register #(.width(32)) register_1 (.D(in_1), .en(WE), .clk(CLK), .Q(out_5), .clr(CLR));
endmodule

module mux2 (
  input  [31:0] A,
  input  [31:0] B,
  input  Sel,
  output [31:0] Selected
);

  Multiplexer #(.enable("true"), .width(32)) multiplexer_1 (.in0(A), .in1(B), .out(Selected), .sel(Sel));  // open: en
endmodule

module mux3 (
  input  [31:0] A,
  input  [31:0] B,
  input  [31:0] C,
  input  [1:0] Sel,
  output [31:0] Selected
);

  Multiplexer #(.enable("true"), .select(2), .width(32)) multiplexer_1 (
    .in0(A), .in1(B), .in2(C), .out(Selected), .sel(Sel));  // open: in3, en
endmodule

module mux4 (
  input  [31:0] A,
  input  [31:0] B,
  input  [31:0] C,
  input  [31:0] D,
  input  [1:0] Sel,
  output [31:0] Selected
);

  Multiplexer #(.enable("true"), .select(2), .width(32)) multiplexer_1 (
    .in0(A), .in1(B), .in2(C), .in3(D), .out(Selected), .sel(Sel));  // open: en
endmodule

module regfile (
  input  [4:0] A1,
  input  [4:0] A2,
  input  [4:0] A3,
  input  [31:0] WD3,
  input  WE3,
  input  CLK,
  output [31:0] RD1,
  output [31:0] RD2
);

  wire w0, w1, w2, w3, w4, w5, w6, w7, w8, w9, w10, w11, w12, w13, w14, w15, w16, w17, w18, w19, w20, w21,
       w22, w23, w24, w25, w26, w27, w28, w29, w30, w31, wr0, wr1, wr2, wr3, wr4, wr5, wr6, wr7, wr8, wr9,
       wr10, wr11, wr12, wr13, wr14, wr15, wr16, wr17, wr18, wr19, wr20, wr21, wr22, wr23, wr24, wr25, wr26,
       wr27, wr28, wr29, wr30, wr31;
  wire [31:0] o0, o1, o2, o3, o4, o5, o6, o7, o8, o9, o10, o11, o12, o13, o14, o15, o16, o17, o18, o19, o20,
       o21, o22, o23, o24, o25, o26, o27, o28, o29, o30, o31;

  Decoder #(.select(5)) decoder_1 (
    .out0(wr0), .out1(wr1), .out2(wr2), .out3(wr3), .out4(wr4), .out5(wr5), .out6(wr6), .out7(wr7),
    .out8(wr8), .out9(wr9), .out10(wr10), .out11(wr11), .out12(wr12), .out13(wr13), .out14(wr14),
    .out15(wr15), .out16(wr16), .out17(wr17), .out18(wr18), .out19(wr19), .out20(wr20), .out21(wr21),
    .out22(wr22), .out23(wr23), .out24(wr24), .out25(wr25), .out26(wr26), .out27(wr27), .out28(wr28),
    .out29(wr29), .out30(wr30), .out31(wr31), .sel(A3));  // open: en
  Register #(.width(32)) x0 (.D(WD3), .en(w0), .clk(CLK), .Q(o0), .clr(1'b1));
  Register #(.width(32)) x1 (.D(WD3), .en(w1), .clk(CLK), .Q(o1), .clr(1'b0));
  Register #(.width(32)) x2 (.D(WD3), .en(w2), .clk(CLK), .Q(o2), .clr(1'b0));
  Register #(.width(32)) x3 (.D(WD3), .en(w3), .clk(CLK), .Q(o3), .clr(1'b0));
  Register #(.width(32)) x4 (.D(WD3), .en(w4), .clk(CLK), .Q(o4), .clr(1'b0));
  Register #(.width(32)) x5 (.D(WD3), .en(w5), .clk(CLK), .Q(o5), .clr(1'b0));
  Register #(.width(32)) x6 (.D(WD3), .en(w6), .clk(CLK), .Q(o6), .clr(1'b0));
  Register #(.width(32)) x7 (.D(WD3), .en(w7), .clk(CLK), .Q(o7), .clr(1'b0));
  Register #(.width(32)) x8 (.D(WD3), .en(w8), .clk(CLK), .Q(o8), .clr(1'b0));
  Register #(.width(32)) x9 (.D(WD3), .en(w9), .clk(CLK), .Q(o9), .clr(1'b0));
  Register #(.width(32)) x10 (.D(WD3), .en(w10), .clk(CLK), .Q(o10), .clr(1'b0));
  Register #(.width(32)) x11 (.D(WD3), .en(w11), .clk(CLK), .Q(o11), .clr(1'b0));
  Register #(.width(32)) x12 (.D(WD3), .en(w12), .clk(CLK), .Q(o12), .clr(1'b0));
  Register #(.width(32)) x13 (.D(WD3), .en(w13), .clk(CLK), .Q(o13), .clr(1'b0));
  Register #(.width(32)) x14 (.D(WD3), .en(w14), .clk(CLK), .Q(o14), .clr(1'b0));
  Register #(.width(32)) x15 (.D(WD3), .en(w15), .clk(CLK), .Q(o15), .clr(1'b0));
  Register #(.width(32)) x16 (.D(WD3), .en(w16), .clk(CLK), .Q(o16), .clr(1'b0));
  Register #(.width(32)) x17 (.D(WD3), .en(w17), .clk(CLK), .Q(o17), .clr(1'b0));
  Register #(.width(32)) x18 (.D(WD3), .en(w18), .clk(CLK), .Q(o18), .clr(1'b0));
  Register #(.width(32)) x19 (.D(WD3), .en(w19), .clk(CLK), .Q(o19), .clr(1'b0));
  Register #(.width(32)) x20 (.D(WD3), .en(w20), .clk(CLK), .Q(o20), .clr(1'b0));
  Register #(.width(32)) x21 (.D(WD3), .en(w21), .clk(CLK), .Q(o21), .clr(1'b0));
  Register #(.width(32)) x22 (.D(WD3), .en(w22), .clk(CLK), .Q(o22), .clr(1'b0));
  Register #(.width(32)) x23 (.D(WD3), .en(w23), .clk(CLK), .Q(o23), .clr(1'b0));
  and and_1 (w0, wr0, WE3);
  and and_2 (w1, wr1, WE3);
  and and_3 (w2, wr2, WE3);
  and and_4 (w3, wr3, WE3);
  and and_5 (w4, wr4, WE3);
  and and_6 (w5, wr5, WE3);
  and and_7 (w6, wr6, WE3);
  and and_8 (w7, wr7, WE3);
  Register #(.width(32)) x24 (.D(WD3), .en(w24), .clk(CLK), .Q(o24), .clr(1'b0));
  Register #(.width(32)) x25 (.D(WD3), .en(w25), .clk(CLK), .Q(o25), .clr(1'b0));
  Register #(.width(32)) x26 (.D(WD3), .en(w26), .clk(CLK), .Q(o26), .clr(1'b0));
  Register #(.width(32)) x27 (.D(WD3), .en(w27), .clk(CLK), .Q(o27), .clr(1'b0));
  Register #(.width(32)) x28 (.D(WD3), .en(w28), .clk(CLK), .Q(o28), .clr(1'b0));
  Register #(.width(32)) x29 (.D(WD3), .en(w29), .clk(CLK), .Q(o29), .clr(1'b0));
  Register #(.width(32)) x30 (.D(WD3), .en(w30), .clk(CLK), .Q(o30), .clr(1'b0));
  Register #(.width(32)) x31 (.D(WD3), .en(w31), .clk(CLK), .Q(o31), .clr(1'b0));
  and and_9 (w8, wr8, WE3);
  and and_10 (w9, wr9, WE3);
  and and_11 (w10, wr10, WE3);
  and and_12 (w11, wr11, WE3);
  and and_13 (w12, wr12, WE3);
  and and_14 (w13, wr13, WE3);
  and and_15 (w14, wr14, WE3);
  and and_16 (w15, wr15, WE3);
  and and_17 (w16, wr16, WE3);
  and and_18 (w17, wr17, WE3);
  and and_19 (w18, wr18, WE3);
  and and_20 (w19, wr19, WE3);
  and and_21 (w20, wr20, WE3);
  and and_22 (w21, wr21, WE3);
  and and_23 (w22, wr22, WE3);
  and and_24 (w23, wr23, WE3);
  and and_25 (w24, wr24, WE3);
  and and_26 (w25, wr25, WE3);
  and and_27 (w26, wr26, WE3);
  and and_28 (w27, wr27, WE3);
  and and_29 (w28, wr28, WE3);
  and and_30 (w29, wr29, WE3);
  and and_31 (w30, wr30, WE3);
  and and_32 (w31, wr31, WE3);
  Multiplexer #(.enable("true"), .select(5), .width(32)) multiplexer_1 (
    .in0(o0), .in1(o1), .in2(o2), .in3(o3), .in4(o4), .in5(o5), .in6(o6), .in7(o7), .in8(o8), .in9(o9),
    .in10(o10), .in11(o11), .in12(o12), .in13(o13), .in14(o14), .in15(o15), .in16(o16), .in17(o17),
    .in18(o18), .in19(o19), .in20(o20), .in21(o21), .in22(o22), .in23(o23), .in24(o24), .in25(o25),
    .in26(o26), .in27(o27), .in28(o28), .in29(o29), .in30(o30), .in31(o31), .out(RD1), .sel(A1));  // open: en
  Multiplexer #(.enable("true"), .select(5), .width(32)) multiplexer_2 (
    .in0(o0), .in1(o1), .in2(o2), .in3(o3), .in4(o4), .in5(o5), .in6(o6), .in7(o7), .in8(o8), .in9(o9),
    .in10(o10), .in11(o11), .in12(o12), .in13(o13), .in14(o14), .in15(o15), .in16(o16), .in17(o17),
    .in18(o18), .in19(o19), .in20(o20), .in21(o21), .in22(o22), .in23(o23), .in24(o24), .in25(o25),
    .in26(o26), .in27(o27), .in28(o28), .in29(o29), .in30(o30), .in31(o31), .out(RD2), .sel(A2));  // open: en
endmodule

module extend (
  input  [24:0] Instr31_7,
  input  [2:0] ImmSrc,
  output [31:0] ImmExt
);

  wire [31:0] BTypeImm, ITypeImm, JTypeImm, STypeImm;

  // Probe on ITypeImm
  assign ITypeImm = {{20{Instr31_7[24]}}, Instr31_7[24:13]};  // Bit_Extender bit_extender_1
  // Probe on BTypeImm
  assign BTypeImm = {{19{Instr31_7[24]}}, {Instr31_7[24], Instr31_7[0], Instr31_7[23:18], Instr31_7[4:1], 1'b0}};  // Bit_Extender bit_extender_2
  // Probe on STypeImm
  assign STypeImm = {{20{Instr31_7[24]}}, {Instr31_7[24:18], Instr31_7[4:0]}};  // Bit_Extender bit_extender_3
  // Probe on {Instr31_7[24:5], {12{1'b0}}}
  Multiplexer #(.enable("true"), .select(3), .width(32)) multiplexer_1 (
    .in0(ITypeImm), .in1(STypeImm), .in2(BTypeImm), .in3(JTypeImm), .in4({Instr31_7[24:5], {12{1'b0}}}),
    .out(ImmExt), .sel(ImmSrc));  // open: in5, in6, in7, en
  // Probe on JTypeImm
  assign JTypeImm = {{11{Instr31_7[24]}}, {Instr31_7[24], Instr31_7[12:5], Instr31_7[13], Instr31_7[23:14], 1'b0}};  // Bit_Extender bit_extender_4

  // Other names for the same wires on the sheet: Instr[31:7] = Instr31_7; ITypeImm12[11:0] = Instr31_7[24:13];
  //   JTypeImm21[20:1] = {Instr31_7[24], Instr31_7[12:5], Instr31_7[13], Instr31_7[23:14]};
  //   UTypeImm[31:12] = Instr31_7[24:5];
  //   BTypeImm13[12:1] = {Instr31_7[24], Instr31_7[0], Instr31_7[23:18], Instr31_7[4:1]};
  //   STypeImm12[11:0] = {Instr31_7[24:18], Instr31_7[4:0]}

  // Notes on the sheet:
  //   I-type
  //   Input
  //   B-type
  //   S-type
  //   U-type
  //   Output
  //   J-type
endmodule

module adder32 (
  input  [31:0] A,
  input  [31:0] B,
  output [31:0] Sum
);

  Adder #(.width(32)) adder_1 (.a(A), .b(B), .out(Sum));  // open: cin, cout
endmodule

module alu (
  input  [31:0] SrcA,
  input  [31:0] SrcB,
  input  [2:0] ALUControl,
  input  [2:0] Funct3,
  input  Funct7_5,
  output Zero,
  output [31:0] ALUResult,
  output SignedLess,
  output UnsignedLess
);

  wire comparator_4_eq, comparator_5_eq, IsRightShift, IsSLL, IsSRA, IsSRL, not_1_out, or_3_out;
  wire [31:0] adder_1_out, and_1_out, ArithmeticRight, bit_extender_1_out, bit_extender_2_out, LogicalLeft,
       LogicalRight, or_1_out, ShiftResult, ShiftRightOutput, subtractor_1_out, xor_1_out;

  Adder #(.width(32)) adder_1 (.a(SrcA), .b(SrcB), .out(adder_1_out));  // open: cin, cout
  Subtractor #(.width(32)) subtractor_1 (.a(SrcA), .b(SrcB), .out(subtractor_1_out));  // open: bin, bout
  assign and_1_out = SrcA & SrcB;  // AND_Gate and_1, 32 bits wide
  assign or_1_out = SrcA | SrcB;  // OR_Gate or_1, 32 bits wide
  assign xor_1_out = SrcA ^ SrcB;  // XOR_Gate xor_1, 32 bits wide
  Comparator #(.width(32)) comparator_1 (.a(SrcA), .b(SrcB), .lt(SignedLess));  // open: gt, eq
  Comparator #(.mode("unsigned"), .width(32)) comparator_2 (.a(SrcA), .b(SrcB), .lt(UnsignedLess));  // open: gt, eq
  assign bit_extender_1_out = {{31{1'b0}}, UnsignedLess};  // Bit_Extender bit_extender_1
  not not_1 (not_1_out, Funct7_5);
  // Probe on ShiftRightOutput
  Multiplexer #(.width(32)) multiplexer_1 (
    .in0(LogicalRight), .in1(ArithmeticRight), .out(ShiftRightOutput), .sel(IsSRA));
  assign bit_extender_2_out = {{31{1'b0}}, SignedLess};  // Bit_Extender bit_extender_2
  Comparator #(.mode("unsigned"), .width(3)) comparator_3 (.a(Funct3), .b(3'b001), .eq(IsSLL));  // open: gt, lt
  Comparator #(.mode("unsigned"), .width(3)) comparator_4 (
    .a(Funct3), .b(3'b101), .eq(comparator_4_eq));  // open: gt, lt
  Comparator #(.mode("unsigned"), .width(3)) comparator_5 (
    .a(Funct3), .b(3'b101), .eq(comparator_5_eq));  // open: gt, lt
  Shifter #(.width(32)) shifter_1 (.in(SrcA), .\dist (SrcB[4:0]), .out(LogicalLeft));
  Shifter #(.shift("lr"), .width(32)) shifter_2 (.in(SrcA), .\dist (SrcB[4:0]), .out(LogicalRight));
  Shifter #(.shift("ar"), .width(32)) shifter_3 (.in(SrcA), .\dist (SrcB[4:0]), .out(ArithmeticRight));
  and and_2 (IsSRL, comparator_4_eq, not_1_out);
  and and_3 (IsSRA, comparator_5_eq, Funct7_5);
  Multiplexer #(.enable("true"), .select(3), .width(32)) multiplexer_2 (
    .in0(adder_1_out), .in1(subtractor_1_out), .in2(and_1_out), .in3(or_1_out), .in4(xor_1_out),
    .in5(bit_extender_2_out), .in6(ShiftResult), .in7(bit_extender_1_out), .out(ALUResult), .sel(ALUControl));  // open: en
  // Probe on ALUControl
  or or_2 (IsRightShift, IsSRL, IsSRA);
  // Probe on ShiftResult
  Multiplexer #(.width(32)) multiplexer_3 (
    .in0(LogicalLeft), .in1(ShiftRightOutput), .out(ShiftResult), .sel(IsRightShift));
  or or_3 (or_3_out, ALUResult[0], ALUResult[1], ALUResult[2], ALUResult[3], ALUResult[4], ALUResult[5], ALUResult[6], ALUResult[7], ALUResult[8], ALUResult[9], ALUResult[10], ALUResult[11], ALUResult[12], ALUResult[13], ALUResult[14], ALUResult[15], ALUResult[17], ALUResult[18], ALUResult[19], ALUResult[20], ALUResult[21], ALUResult[22], ALUResult[23], ALUResult[24], ALUResult[25], ALUResult[26], ALUResult[27], ALUResult[28], ALUResult[29], ALUResult[30], ALUResult[31], ALUResult[16]);
  not not_2 (Zero, or_3_out);

  // Other names for the same wires on the sheet: ALUResultSign = ALUResult[31]; shamt[4:0] = SrcB[4:0]

  // Notes on the sheet:
  //   Input
  //   ALUResult
  //   SHIFTER Logic
  //   Output
  //   Zero
endmodule

module nextstatelogic (
  input  [6:0] opcode,
  input  [3:0] State,
  input  [2:0] funct3,
  output [3:0] NextState
);

  wire IsAUIPC, IsBType, IsITypeALU, IsJAL, IsJAL8, IsLoad, IsLUI, IsRType, IsStore;
  wire [2:0] Selector;
  wire [3:0] NextS1, NextS2;

  Multiplexer #(.enable("true"), .select(3), .width(4)) multiplexer_1 (
    .in0(4'b0011), .in1(4'b0101), .out(NextS2), .sel(Selector));  // open: in2, in3, in4, in5, in6, in7, en
  Multiplexer #(.enable("true"), .select(3), .width(4)) multiplexer_2 (
    .in0(4'b0010), .in1(4'b0010), .in2(4'b0110), .in3(4'b1010), .in4(4'b1000), .in5(4'b1001), .in6(4'b1011),
    .in7(4'b1100), .out(NextS1), .sel(Selector));  // open: en
  Comparator #(.mode("unsigned"), .width(7)) comparator_1 (.a(opcode), .b(7'b0000011), .eq(IsLoad));  // open: gt, lt
  Comparator #(.mode("unsigned"), .width(7)) comparator_2 (.a(opcode), .b(7'b0100011), .eq(IsStore));  // open: gt, lt
  Comparator #(.mode("unsigned"), .width(7)) comparator_3 (.a(opcode), .b(7'b0110011), .eq(IsRType));  // open: gt, lt
  Comparator #(.mode("unsigned"), .width(7)) comparator_4 (.a(opcode), .b(7'b1100011), .eq(IsBType));  // open: gt, lt
  Comparator #(.mode("unsigned"), .width(7)) comparator_5 (
    .a(opcode), .b(7'b0010011), .eq(IsITypeALU));  // open: gt, lt
  Comparator #(.mode("unsigned"), .width(7)) comparator_6 (.a(opcode), .b(7'b1101111), .eq(IsJAL));  // open: gt, lt
  Comparator #(.mode("unsigned"), .width(7)) comparator_7 (.a(opcode), .b(7'b1101110), .eq(IsJAL8));  // open: gt, lt
  Comparator #(.mode("unsigned"), .width(7)) comparator_8 (.a(opcode), .b(7'b0010111), .eq(IsAUIPC));  // open: gt, lt
  Comparator #(.mode("unsigned"), .width(7)) comparator_9 (.a(opcode), .b(7'b0110111), .eq(IsLUI));  // open: gt, lt
  Multiplexer #(.enable("true"), .select(4), .width(4)) multiplexer_3 (
    .in0(4'b0001), .in1(NextS1), .in2(NextS2), .in3(4'b0100), .in4(4'b0000), .in5(4'b0000), .in6(4'b0111),
    .in7(4'b0000), .in8(4'b0111), .in9(4'b0111), .in10(4'b0000), .in11(4'b0111), .in12(4'b0000),
    .out(NextState), .sel(State));  // open: in13, in14, in15, en
  // Probe on NextState
  Priority_Encoder priority_encoder_1 (
    .in0(IsLoad), .in1(IsStore), .in2(IsRType), .in3(IsBType), .in4(IsITypeALU), .in5(IsJAL), .in6(IsJAL8),
    .in7(IsLUI), .out(Selector));  // open: en_in, gs, en_out
  // Probe on Selector
endmodule

module instrdecoder (
  input  [6:0] opcode,
  output [2:0] ImmSrc
);

  wire IsAUIPC, IsBEQ, IsITypeALU, IsJAL, IsJAL8, IsLoad, IsLUI, IsRType, IsStore;
  wire [2:0] Selector, undriven;

  Comparator #(.mode("unsigned"), .width(7)) comparator_1 (.a(opcode), .b(7'b0000011), .eq(IsLoad));  // open: gt, lt
  Comparator #(.mode("unsigned"), .width(7)) comparator_2 (.a(opcode), .b(7'b0100011), .eq(IsStore));  // open: gt, lt
  Comparator #(.mode("unsigned"), .width(7)) comparator_3 (.a(opcode), .b(7'b0110011), .eq(IsRType));  // open: gt, lt
  Comparator #(.mode("unsigned"), .width(7)) comparator_4 (.a(opcode), .b(7'b1100011), .eq(IsBEQ));  // open: gt, lt
  Comparator #(.mode("unsigned"), .width(7)) comparator_5 (
    .a(opcode), .b(7'b0010011), .eq(IsITypeALU));  // open: gt, lt
  Comparator #(.mode("unsigned"), .width(7)) comparator_6 (.a(opcode), .b(7'b1101111), .eq(IsJAL));  // open: gt, lt
  Comparator #(.mode("unsigned"), .width(7)) comparator_7 (.a(opcode), .b(7'b1101110), .eq(IsJAL8));  // open: gt, lt
  Comparator #(.mode("unsigned"), .width(7)) comparator_8 (.a(opcode), .b(7'b0010111), .eq(IsAUIPC));  // open: gt, lt
  Comparator #(.mode("unsigned"), .width(7)) comparator_9 (.a(opcode), .b(7'b0110111), .eq(IsLUI));  // open: gt, lt
  // Probe on ImmSrc
  Multiplexer #(.enable("true"), .select(3), .width(3)) multiplexer_1 (
    .in0(3'b000), .in1(3'b001), .in2(undriven), .in3(3'b010), .in4(3'b000), .in5(3'b011), .in6(3'b011),
    .in7(3'b100), .out(ImmSrc), .sel(Selector));  // open: en
  Priority_Encoder priority_encoder_1 (
    .in0(IsLoad), .in1(IsStore), .in2(IsRType), .in3(IsBEQ), .in4(IsITypeALU), .in5(IsJAL), .in6(IsJAL8),
    .in7(IsLUI), .out(Selector));  // open: en_in, gs, en_out
  // Probe on Selector
endmodule

module instmem (
  input  [31:0] Address,
  output [31:0] Instr
);

  ROM #(.dataWidth(32)) InstMem (.addr(Address[9:2]), .data(Instr));

  // Notes on the sheet:
  //   // Nasty hack to make word-addressable ROM usable
  //   contents of InstMem (hex, n*v repeats v):
  //   500093 500113 209463 100193 200213
endmodule

module maindecoder (
  input  [3:0] state,
  output PCUpdate,
  output Branch,
  output MemWrite,
  output IRWrite,
  output RegWrite,
  output AdrSrc,
  output [1:0] ALUSrcA,
  output [1:0] ALUSrcB,
  output [1:0] ResultSrc,
  output [1:0] ALUOp
);

  Multiplexer #(.enable("true"), .select(4)) multiplexer_1 (
    .in0(1'b1), .in1(1'b0), .in2(1'b0), .in3(1'b0), .in4(1'b0), .in5(1'b0), .in6(1'b0), .in7(1'b0),
    .in8(1'b0), .in9(1'b1), .in10(1'b0), .in11(1'b1), .in12(1'b0), .out(PCUpdate), .sel(state));  // open: in13, in14, in15, en
  Multiplexer #(.enable("true"), .select(4)) multiplexer_2 (
    .in0(1'b0), .in1(1'b0), .in2(1'b0), .in3(1'b0), .in4(1'b0), .in5(1'b0), .in6(1'b0), .in7(1'b0),
    .in8(1'b0), .in9(1'b0), .in10(1'b1), .in11(1'b0), .in12(1'b0), .out(Branch), .sel(state));  // open: in13, in14, in15, en
  Multiplexer #(.enable("true"), .select(4)) multiplexer_3 (
    .in0(1'b0), .in1(1'b0), .in2(1'b0), .in3(1'b0), .in4(1'b0), .in5(1'b1), .in6(1'b0), .in7(1'b0),
    .in8(1'b0), .in9(1'b0), .in10(1'b0), .in11(1'b0), .in12(1'b0), .out(MemWrite), .sel(state));  // open: in13, in14, in15, en
  Multiplexer #(.enable("true"), .select(4)) multiplexer_4 (
    .in0(1'b1), .in1(1'b0), .in2(1'b0), .in3(1'b0), .in4(1'b0), .in5(1'b0), .in6(1'b0), .in7(1'b0),
    .in8(1'b0), .in9(1'b0), .in10(1'b0), .in11(1'b0), .in12(1'b0), .out(IRWrite), .sel(state));  // open: in13, in14, in15, en
  Multiplexer #(.enable("true"), .select(4)) multiplexer_5 (
    .in0(1'b0), .in1(1'b0), .in2(1'b0), .in3(1'b0), .in4(1'b1), .in5(1'b0), .in6(1'b0), .in7(1'b1),
    .in8(1'b0), .in9(1'b0), .in10(1'b0), .in11(1'b0), .in12(1'b1), .out(RegWrite), .sel(state));  // open: in13, in14, in15, en
  Multiplexer #(.enable("true"), .select(4)) multiplexer_6 (
    .in0(1'b0), .in2(1'b0), .in3(1'b1), .in4(1'b0), .in5(1'b1), .in11(1'b1), .out(AdrSrc), .sel(state));  // open: in1, in6, in7, in8, in9, in10, in12, in13, in14, in15, en
  Multiplexer #(.enable("true"), .select(4), .width(2)) multiplexer_7 (
    .in0(2'b00), .in1(2'b01), .in2(2'b10), .in6(2'b10), .in8(2'b10), .in9(2'b01), .in10(2'b10), .in11(2'b00),
    .out(ALUSrcA), .sel(state));  // open: in3, in4, in5, in7, in12, in13, in14, in15, en
  Multiplexer #(.enable("true"), .select(4), .width(2)) multiplexer_8 (
    .in0(2'b10), .in1(2'b01), .in2(2'b01), .in6(2'b00), .in8(2'b01), .in9(2'b10), .in10(2'b00), .in11(2'b10),
    .out(ALUSrcB), .sel(state));  // open: in3, in4, in5, in7, in12, in13, in14, in15, en
  Multiplexer #(.enable("true"), .select(4), .width(2)) multiplexer_9 (
    .in0(2'b00), .in1(2'b00), .in2(2'b00), .in6(2'b10), .in8(2'b10), .in9(2'b00), .in10(2'b01), .in11(2'b00),
    .out(ALUOp), .sel(state));  // open: in3, in4, in5, in7, in12, in13, in14, in15, en
  Multiplexer #(.enable("true"), .select(4), .width(2)) multiplexer_10 (
    .in0(2'b10), .in3(2'b00), .in4(2'b01), .in5(2'b00), .in7(2'b00), .in9(2'b00), .in10(2'b00), .in11(2'b00),
    .in12(2'b11), .out(ResultSrc), .sel(state));  // open: in1, in2, in6, in8, in13, in14, in15, en

  // Notes on the sheet:
  //   Input
  //   Control Signals
  //   EXPERIMENT: S4 = 0
  //   Output
  //   EXPERIMENT: S4 = 1
endmodule

module aludecoder (
  input  funct7_5,
  input  [2:0] funct3,
  input  [1:0] ALUOp,
  input  [6:0] opcode,
  output [2:0] ALUControl
);

  wire and_1_out, and_2_out, comparator_1_eq, comparator_2_eq, comparator_3_eq, comparator_4_eq,
       comparator_5_eq, comparator_6_eq, comparator_7_eq, comparator_8_eq, comparator_9_eq, comparator_10_eq,
       comparator_11_eq, comparator_12_eq, comparator_13_eq, comparator_14_eq, comparator_15_eq,
       comparator_16_eq, comparator_17_eq, comparator_18_eq, comparator_19_eq, comparator_20_eq,
       comparator_21_eq, comparator_22_eq, comparator_23_eq, comparator_24_eq, IsAdd, IsAnd, IsOr, IsShift,
       IsSLL, IsSLT, IsSLTU, IsSRA, IsSRL, IsSub, IsXor, not_1_out, not_2_out;

  Comparator #(.mode("unsigned"), .width(2)) comparator_1 (.a(ALUOp), .b(2'b10), .eq(comparator_1_eq));  // open: gt, lt
  Comparator #(.mode("unsigned"), .width(3)) comparator_2 (
    .a(funct3), .b(3'b100), .eq(comparator_2_eq));  // open: gt, lt
  Comparator #(.mode("unsigned"), .width(2)) comparator_3 (.a(ALUOp), .b(2'b10), .eq(comparator_3_eq));  // open: gt, lt
  Comparator #(.mode("unsigned"), .width(3)) comparator_4 (
    .a(funct3), .b(3'b011), .eq(comparator_4_eq));  // open: gt, lt
  Comparator #(.mode("unsigned"), .width(2)) comparator_5 (.a(ALUOp), .b(2'b00), .eq(comparator_5_eq));  // open: gt, lt
  Comparator #(.mode("unsigned"), .width(2)) comparator_6 (.a(ALUOp), .b(2'b10), .eq(comparator_6_eq));  // open: gt, lt
  Comparator #(.mode("unsigned"), .width(3)) comparator_7 (
    .a(funct3), .b(3'b000), .eq(comparator_7_eq));  // open: gt, lt
  not not_1 (not_1_out, comparator_8_eq);
  Comparator #(.mode("unsigned"), .width(2)) comparator_8 (
    .a({opcode[5], funct7_5}), .b(2'b11), .eq(comparator_8_eq));  // open: gt, lt
  Comparator #(.mode("unsigned"), .width(2)) comparator_9 (.a(ALUOp), .b(2'b01), .eq(comparator_9_eq));  // open: gt, lt
  Comparator #(.mode("unsigned"), .width(2)) comparator_10 (
    .a(ALUOp), .b(2'b10), .eq(comparator_10_eq));  // open: gt, lt
  Comparator #(.mode("unsigned"), .width(3)) comparator_11 (
    .a(funct3), .b(3'b000), .eq(comparator_11_eq));  // open: gt, lt
  Comparator #(.mode("unsigned"), .width(2)) comparator_12 (
    .a({opcode[5], funct7_5}), .b(2'b11), .eq(comparator_12_eq));  // open: gt, lt
  Comparator #(.mode("unsigned"), .width(2)) comparator_13 (
    .a(ALUOp), .b(2'b10), .eq(comparator_13_eq));  // open: gt, lt
  Comparator #(.mode("unsigned"), .width(3)) comparator_14 (
    .a(funct3), .b(3'b010), .eq(comparator_14_eq));  // open: gt, lt
  Comparator #(.mode("unsigned"), .width(2)) comparator_15 (
    .a(ALUOp), .b(2'b10), .eq(comparator_15_eq));  // open: gt, lt
  Comparator #(.mode("unsigned"), .width(3)) comparator_16 (
    .a(funct3), .b(3'b110), .eq(comparator_16_eq));  // open: gt, lt
  Comparator #(.mode("unsigned"), .width(2)) comparator_17 (
    .a(ALUOp), .b(2'b10), .eq(comparator_17_eq));  // open: gt, lt
  Comparator #(.mode("unsigned"), .width(3)) comparator_18 (
    .a(funct3), .b(3'b111), .eq(comparator_18_eq));  // open: gt, lt
  and and_1 (and_1_out, comparator_6_eq, comparator_7_eq, not_1_out);
  or or_1 (IsSub, comparator_9_eq, and_2_out);
  and and_2 (and_2_out, comparator_10_eq, comparator_11_eq, comparator_12_eq);
  and and_3 (IsSLT, comparator_13_eq, comparator_14_eq);
  and and_4 (IsOr, comparator_15_eq, comparator_16_eq);
  and and_5 (IsAnd, comparator_17_eq, comparator_18_eq);
  and and_6 (IsXor, comparator_1_eq, comparator_2_eq);
  and and_7 (IsSLTU, comparator_3_eq, comparator_4_eq);
  or or_2 (IsAdd, comparator_5_eq, and_1_out);
  Priority_Encoder priority_encoder_1 (
    .in0(IsAdd), .in1(IsSub), .in2(IsAnd), .in3(IsOr), .in4(IsXor), .in5(IsSLT), .in6(IsShift), .in7(IsSLTU),
    .out(ALUControl));  // open: en_in, gs, en_out
  Comparator #(.mode("unsigned"), .width(2)) comparator_19 (
    .a(ALUOp), .b(2'b10), .eq(comparator_19_eq));  // open: gt, lt
  Comparator #(.mode("unsigned"), .width(3)) comparator_20 (
    .a(funct3), .b(3'b001), .eq(comparator_20_eq));  // open: gt, lt
  Comparator #(.mode("unsigned"), .width(2)) comparator_21 (
    .a(ALUOp), .b(2'b10), .eq(comparator_21_eq));  // open: gt, lt
  Comparator #(.mode("unsigned"), .width(3)) comparator_22 (
    .a(funct3), .b(3'b101), .eq(comparator_22_eq));  // open: gt, lt
  Comparator #(.mode("unsigned"), .width(2)) comparator_23 (
    .a(ALUOp), .b(2'b10), .eq(comparator_23_eq));  // open: gt, lt
  Comparator #(.mode("unsigned"), .width(3)) comparator_24 (
    .a(funct3), .b(3'b101), .eq(comparator_24_eq));  // open: gt, lt
  or or_3 (IsShift, IsSLL, IsSRL, IsSRA);
  and and_8 (IsSLL, comparator_19_eq, comparator_20_eq);
  not not_2 (not_2_out, funct7_5);
  and and_9 (IsSRA, comparator_23_eq, comparator_24_eq, funct7_5);
  and and_10 (IsSRL, comparator_21_eq, comparator_22_eq, not_2_out);

  // Other names for the same wires on the sheet: concat[1:0] = {opcode[5], funct7_5}; opcode_5 = opcode[5]
endmodule

module instsplitter (
  input  [31:0] Instr,
  output [6:0] Instr6_0,
  output [2:0] Instr14_12,
  output Instr30,
  output [4:0] Instr19_15,
  output [4:0] Instr24_20,
  output [4:0] Instr11_7,
  output [24:0] Instr31_7
);


  assign Instr6_0 = Instr[6:0];
  assign Instr11_7 = Instr[11:7];
  assign Instr14_12 = Instr[14:12];
  assign Instr19_15 = Instr[19:15];
  assign Instr24_20 = Instr[24:20];
  assign Instr30 = Instr[30];
  assign Instr31_7 = Instr[31:7];
endmodule

module BranchLogic (
  input  Branch,
  input  Zero,
  input  SignedLess,
  input  UnsignedLess,
  input  [2:0] Funct3,
  output BranchTaken
);

  wire BEQTaken, BGETaken, BGEUTaken, BLTTaken, BLTUTaken, BNETaken, IsBEQ, IsBGE, IsBGEU, IsBLT, IsBLTU,
       IsBNE, not_1_out, not_2_out, not_3_out, or_1_out;

  Comparator #(.mode("unsigned"), .width(3)) comparator_1 (.a(Funct3), .b(3'b000), .eq(IsBEQ));  // open: gt, lt
  Comparator #(.mode("unsigned"), .width(3)) comparator_2 (.a(Funct3), .b(3'b001), .eq(IsBNE));  // open: gt, lt
  Comparator #(.mode("unsigned"), .width(3)) comparator_3 (.a(Funct3), .b(3'b100), .eq(IsBLT));  // open: gt, lt
  Comparator #(.mode("unsigned"), .width(3)) comparator_4 (.a(Funct3), .b(3'b101), .eq(IsBGE));  // open: gt, lt
  Comparator #(.mode("unsigned"), .width(3)) comparator_5 (.a(Funct3), .b(3'b110), .eq(IsBLTU));  // open: gt, lt
  Comparator #(.mode("unsigned"), .width(3)) comparator_6 (.a(Funct3), .b(3'b111), .eq(IsBGEU));  // open: gt, lt
  not not_1 (not_1_out, Zero);
  not not_2 (not_2_out, SignedLess);
  and and_1 (BEQTaken, IsBEQ, Zero);
  and and_2 (BNETaken, IsBNE, not_1_out);
  and and_3 (BLTTaken, IsBLT, SignedLess);
  and and_4 (BGETaken, IsBGE, not_2_out);
  not not_3 (not_3_out, UnsignedLess);
  or or_1 (or_1_out, BEQTaken, BNETaken, BLTTaken, BGETaken, BLTUTaken, BGEUTaken);
  and and_5 (BLTUTaken, IsBLTU, UnsignedLess);
  and and_6 (BGEUTaken, IsBGEU, not_3_out);
  and and_7 (BranchTaken, or_1_out, Branch);
endmodule

module LoadFormatter (
  input  [31:0] MemData,
  input  [1:0] Addr_1_0,
  input  [2:0] Funct3,
  output [31:0] LoadData
);

  wire [7:0] ChosenByte;
  wire [15:0] ChosenHalfword;
  wire [31:0] LB, LBU, LH, LHU;

  // Probe on ChosenByte
  Multiplexer #(.enable("true"), .select(2), .width(8)) multiplexer_1 (
    .in0(MemData[7:0]), .in1(MemData[15:8]), .in2(MemData[23:16]), .in3(MemData[31:24]), .out(ChosenByte),
    .sel(Addr_1_0));  // open: en
  // Probe on ChosenHalfword
  Multiplexer #(.width(16)) multiplexer_2 (
    .in0(MemData[15:0]), .in1(MemData[31:16]), .out(ChosenHalfword), .sel(Addr_1_0[1]));
  // Probe on LB
  Multiplexer #(.select(3), .width(32)) multiplexer_3 (
    .in0(LB), .in1(LH), .in2(MemData), .in4(LBU), .in5(LHU), .out(LoadData), .sel(Funct3));  // open: in3, in6, in7
  assign LB = {{24{ChosenByte[7]}}, ChosenByte};  // Bit_Extender bit_extender_1
  assign LBU = {{24{1'b0}}, ChosenByte};  // Bit_Extender bit_extender_2
  assign LH = {{16{ChosenHalfword[15]}}, ChosenHalfword};  // Bit_Extender bit_extender_3
  assign LHU = {{16{1'b0}}, ChosenHalfword};  // Bit_Extender bit_extender_4
  // Probe on LB
  // Probe on LBU
  // Probe on LH
  // Probe on LHU

  // Other names for the same wires on the sheet: LW[31:0] = MemData
endmodule

module StoreFormatter (
  input  [31:0] MemData,
  input  [31:0] WriteData,
  input  [1:0] Addr_1_0,
  input  [2:0] Funct3,
  output [31:0] StoreData
);

  wire [31:0] SB, SH;

  // Probe on WriteData[7:0]
  // Probe on SB
  Multiplexer #(.enable("true"), .select(2), .width(32)) multiplexer_1 (
    .in0({{24{1'b0}}, WriteData[7:0]}), .in1({{16{1'b0}}, WriteData[7:0], {8{1'b0}}}),
    .in2({{8{1'b0}}, WriteData[7:0], {16{1'b0}}}), .in3({WriteData[7:0], {24{1'b0}}}), .out(SB),
    .sel(Addr_1_0));  // open: en
  // Probe on SB
  Multiplexer #(.enable("true"), .select(3), .width(32)) multiplexer_2 (
    .in0(SB), .in1(SH), .in2(WriteData), .out(StoreData), .sel(Funct3));  // open: in3, in4, in5, in6, in7, en
  Multiplexer #(.width(32)) multiplexer_3 (
    .in0({{16{1'b0}}, WriteData[15:0]}), .in1({WriteData[15:0], {16{1'b0}}}), .out(SH), .sel(Addr_1_0[1]));

  // Other names for the same wires on the sheet: StoreByte[7:0] = WriteData[7:0]; StoreHalf[15:0] = WriteData[15:0];
  //   SW[31:0] = WriteData; ShiftedByte[31:0] = SB; ShiftedHalf[31:0] = SH
endmodule

module UNUSED (
);

  wire [1:0] Addr_1_0;
  wire [31:0] ClearedData_Byte, ClearedData_Half, MemData, SB, SelectedMask_Byte, SelectedMask_Half, SH,
       ShiftedByte, ShiftedHalf;

  Multiplexer #(.width(32)) multiplexer_1 (
    .in0(32'hffff0000), .in1(32'hffff), .out(SelectedMask_Half), .sel(Addr_1_0[1]));
  // Probe on ClearedData_Byte
  assign ClearedData_Byte = MemData & SelectedMask_Byte;  // AND_Gate and_1, 32 bits wide
  assign SB = ClearedData_Byte | ShiftedByte;  // OR_Gate or_1, 32 bits wide
  // Probe on SelectedMask_Byte
  Multiplexer #(.enable("true"), .select(2), .width(32)) multiplexer_2 (
    .in0(32'hffffff00), .in1(32'hffff00ff), .in2(32'hff00ffff), .in3(32'hffffff), .out(SelectedMask_Byte),
    .sel(Addr_1_0));  // open: en
  assign ClearedData_Half = MemData & SelectedMask_Half;  // AND_Gate and_2, 32 bits wide
  assign SH = ClearedData_Half | ShiftedHalf;  // OR_Gate or_2, 32 bits wide
endmodule
